# Fritzing sketch Circuit Project (saved by Fritzing 0.9.2b)
breadboards: 1

parts:
  Part1 = Arduino Uno (Rev3)  # not connected
  Part2 = Arduino Uno (Rev3)  # not connected
  Part3 = Arduino Ethernet Shield (Rev3)
  Part4 = Arduino Ethernet Shield (Rev3)  # not connected
  LED2 = smd LED [color="Red (633nm)" package="1206 [SMD]"]
  LED3 = smd LED [color="Green (565nm)" package="1206 [SMD]"]
  LED4 = smd LED [color="Blue (505nm)" package="1206 [SMD]"]
  LED5 = smd LED [color="Yellow (585nm)" package="1206 [SMD]"]
  R1 = Resistor [tolerance=±5% resistance=1k package="0805 [SMD]"]
  R2 = Resistor [tolerance=±5% resistance=1k package="0805 [SMD]"]
  R3 = Resistor [tolerance=±5% resistance=1k package="0805 [SMD]"]
  R4 = Resistor [tolerance=±5% resistance=1k package="0805 [SMD]"]
  R5 = PHOTOCELL [package=photocell-kit]
  R6 = Resistor [tolerance=±5% resistance=1k package="0805 [SMD]"]

nets:
  N1: Part3.D8, R3.Pin_1
  N2: Part3.PWM_D9, R4.Pin_1
  N3: Part3.A0, R5.P$2, R6.Pin_1
  N4: Part3.D2, R1.Pin_1
  N5: Part3.D7, R2.Pin_1
  N6: Part3.5V, R5.P$1
  N7: Part3.GND, LED2.anode, LED3.anode, LED4.anode, LED5.anode, R6.Pin_0
  N8: LED2.cathode, R1.Pin_0
  N9: LED3.cathode, R2.Pin_0
  N10: LED4.cathode, R3.Pin_0
  N11: LED5.cathode, R4.Pin_0
